# Fritzing sketch assignment 2 (saved by Fritzing 0.9.3b)
breadboards: 1

parts:
  Part1 = Adafruit ADXL343 + ADT7410 Sensor FeatherWing [part_number="Adafruit #4147"]  # not connected
  Part2 = Adafruit 2.13in eInk Under FeatherWing [part_number="Adafruit #4128"]  # not connected
  Part3 = Adafruit HUZZAH32 ESP32 Feather [part_number="Adafruit #3405"]
  PART1 = SparkFun Soil Moisture Sensor [part_number=SEN-13322]
  KEYPAD1 = Membrane Matrix Keypad  # not connected
  hc-sr1 = hc-sr04
  Part4 = Adafruit Adalogger FeatherWing [part_number="Adafruit #2922"]  # not connected
  Part5 = Adafruit DC+Stepper FeatherWing [part_number="Adafruit #2927"]
  J1 = Piezo Speaker
  M1 = DC Motor
  M2 = DC Motor
  J2 = Basic Servo
  BATT1 = 4xAA Switchable Battery Pack w/Bare Wire

nets:
  GND: Part3.GND, PART1.GND, hc-sr1.GND, J1.pin1, J2.gnd
  VCC: Part3.3.3V, PART1.VCC, hc-sr1.VCC, J2.vcc
  N1: Part3.IO12_A11, PART1.SIG
  N2: Part3.IO27_A10, hc-sr1.Trig
  N3: Part3.IO33_A9, hc-sr1.Echo
  N4: Part3.IO15_A8, J1.pin2
  N5: Part3.IO32_A7, J2.pulse
  N6: Part5.GND, BATT1.POS
  N7: Part5.VMOTOR, BATT1.NEG
  N8: Part5.M3B, M2.pin_1
  N9: Part5.M3A, M2.pin_2
  N10: Part5.M4A, M1.pin_1
  N11: Part5.M4B, M1.pin_2

custom parts:
  Adafruit ADXL343 + ADT7410 Sensor FeatherWing: Upgrade any Feather board with motion and precision temperature sensing, with this all-in-one sensing FeatherWing. It sports two fantastic sensors from Analog Devices: an ADXL343 triple-axis accelerometer and an ADT7410 precision temperature sensor. Both sensors are connected over the shared I2C bus, so you can use it with any and all Feathers! We also break out the interrupt pins and address-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
  Adafruit 2.13in eInk Under FeatherWing: Easy e-paper finally comes to your Feather, with this breakout that's designed to make it a breeze to add a tri-color eInk display. Chances are you've seen one of those new-fangled 'e-readers' like the Kindle or Nook. They have gigantic electronic paper 'static' displays - that means the image stays on the display even when power is completely disconnected. The image is also high contrast and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
  SparkFun Soil Moisture Sensor: The SparkFun Soil Moisture Sensor is a simple breakout for measuring the moisture in soil and similar materials.
  Membrane Matrix Keypad: Membrane Matrix 3x4 Keypad
  Adafruit Adalogger FeatherWing: This is the Adalogger FeatherWing: it adds both a battery-backed Real Time Clock and micro SD card storage to any Feather main board. This FeatherWing will make it real easy to add datalogging to any of our existing Feathers. You get both an I2C real time clock (PCF8523) with 32KHz crystal and battery backup, and a microSD socket that connects to the SPI port pins (+ extra pin for CS). Tested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
  Adafruit DC+Stepper FeatherWing: This is the DC Motor + Stepper FeatherWing which will let you use 2 x bi-polar stepper motors or 4 x brushed DC motorx (or 1 stepper and 2 DC motors). Using our Feather Stacking Headers or Feather Female Headers you can connect a FeatherWing on top or bottom of your Feather board and let the board take flight! The original Adafruit Motorshield Kit is one of our most beloved kits, which is why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
  4xAA Switchable Battery Pack w/Bare Wire: 4xAA Switchable Battery Pack with Bare Wire connection
